# Fritzing sketch DeskControl (saved by Fritzing 0.9.4)
circuit board: 6.3cm x 2.7cm
breadboards: 2

parts:
  WeMos_D1_Mini1 = WeMos D1 Mini
  R6 = Resistor [tolerance=±5% resistance=220 package=THT]
  R4 = Resistor [tolerance=±5% resistance=220 package=THT]
  PC817-D = Sharp PC817 [package=THT]
  R7 = Resistor [tolerance=±5% resistance=220 package=THT]
  PC817-D_2 = Sharp PC817 [package=THT]
  R9 = Resistor [tolerance=±5% resistance=10k package=THT]
  HC-SR04_Sensor_1 = HC-SR04 Ultrasonic Distance Sensor
  LED2 = smd LED [color="Green (555nm)" package="1206 [SMD]"]
  LED1 = smd LED [color="Yellow (585nm)" package="1206 [SMD]"]
  J1 = female pin header, 4 pins [form="♀ (female)"]
  R8 = Resistor [tolerance=±5% resistance=10k package=THT]
  RJ45 = RJ45 Jack [package=rj45-8]
  R5 = Resistor [tolerance=±5% resistance=220 package=THT]

nets:
  5V: WeMos_D1_Mini1.5V, R9.Pin_0, HC-SR04_Sensor_1.VCC, R8.Pin_0
  N1: WeMos_D1_Mini1.D0, HC-SR04_Sensor_1.ECHO
  N2: WeMos_D1_Mini1.D1, R9.Pin_1, RJ45.7
  N3: WeMos_D1_Mini1.D2, R8.Pin_1, RJ45.8
  N4: WeMos_D1_Mini1.D3, HC-SR04_Sensor_1.TRIG
  N5: WeMos_D1_Mini1.D5, R4.Pin_1
  N6: WeMos_D1_Mini1.D6, R5.Pin_1
  N7: WeMos_D1_Mini1.D7, R6.Pin_1
  N8: WeMos_D1_Mini1.D8, R7.Pin_1
  N9: WeMos_D1_Mini1.G, PC817-D.Pin_2, PC817-D_2.Pin_2, HC-SR04_Sensor_1.GND, LED2.cathode, LED1.cathode, RJ45.3
  N10: R6.Pin_0, LED2.anode
  N11: R4.Pin_0, PC817-D.Pin_1
  N12: PC817-D.Pin_4, J1.pin3
  N13: PC817-D.Pin_3, J1.pin4
  N14: R7.Pin_0, LED1.anode
  N15: PC817-D_2.Pin_1, R5.Pin_0
  N16: PC817-D_2.Pin_4, J1.pin1
  N17: PC817-D_2.Pin_3, J1.pin2
